# Fritzing sketch tempMonitor (saved by Fritzing 0.9.3b)
breadboards: 1

parts:
  Componente1 = Arduino Uno (Rev3)
  LCD1 = LCD screen
  R1 = Rotary Potentiometer (Small) [maximum_resistance=100kΩ package=THT]
  T1 = LM35 Temperature Sensor [package="TO92 [THT]"]

nets:
  N1: Componente1.A0, T1.Vout
  N2: Componente1.D11_PWM/MOSI, LCD1.E
  N3: Componente1.D12/MISO, LCD1.RS
  N4: Componente1.D2, LCD1.DB7
  N5: Componente1.D3_PWM, LCD1.DB6
  N6: Componente1.D4, LCD1.DB5
  N7: Componente1.D5_PWM, LCD1.DB4
  5V: Componente1.5V, LCD1.VDD, LCD1.LED+, R1.leg1, T1.+Vs
  GND: Componente1.GND, LCD1.VSS, LCD1.R/W, LCD1.LED-, R1.leg2, T1.GND
  N8: LCD1.V0, R1.wiper
